// Logisim project CPU.circ as structural Verilog: 12 circuits, main circuit main
module main (
  input  VCC,
  input  GND,
  input  RESET,
  input  in_4
);

  wire alu_1_cf, alu_1_nf, alu_1_oof, alu_1_zf, and_1_out, and_2_out, and_3_out, and_4_out, CLK_out,
       control_unit_1_bsel, control_unit_1_flags_we, control_unit_1_mar_load, control_unit_1_mem_we,
       control_unit_1_pc_load, control_unit_1_rf_we, flag_register_1_zf, not_1_out, not_2_out, or_1_out,
       or_2_out, or_3_out, tfsm_1_fetch, tfsm_1_ph2, xor_1_out;
  wire [1:0] control_unit_1_rsela, control_unit_1_rselb, control_unit_1_wsel, tfsm_1_t;
  wire [3:0] control_unit_1_alu_op;
  wire [7:0] adder_1_out, alu_1_y, instruction_memory_rom_1_d, instruction_register_1_ir, mar_1_q, mdr_1_q,
       memory_ram_1_d_out, multiplexer_1_out, multiplexer_2_out, multiplexer_3_out, multiplexer_4_out,
       program_counter_1_q, resgister_file_1_aout, resgister_file_1_bout;

  // Probe on mdr_1_q
  Adder adder_1 (.a(program_counter_1_q), .b(8'h1), .out(adder_1_out), .cin(GND));  // open: cout
  Clock CLK (.out(CLK_out));
  Multiplexer #(.width(8)) multiplexer_1 (
    .in0(adder_1_out), .in1(mar_1_q), .out(multiplexer_1_out), .sel(control_unit_1_pc_load));
  or or_1 (or_1_out, tfsm_1_fetch, and_1_out);
  Control_Unit control_unit_1 (
    .IR(instruction_register_1_ir), .ZF(flag_register_1_zf), .T(tfsm_1_t), .RSelB(control_unit_1_rselb),
    .RSelA(control_unit_1_rsela), .ALU_OP(control_unit_1_alu_op), .WSel(control_unit_1_wsel),
    .RF_WE(control_unit_1_rf_we), .BSEL(control_unit_1_bsel), .PC_LOAD(control_unit_1_pc_load),
    .MAR_LOAD(control_unit_1_mar_load), .MEM_WE(control_unit_1_mem_we), .FLAGS_WE(control_unit_1_flags_we));  // open: IR_LOAD, PC_INC, MDR_LOAD, NEEDS2
  MAR mar_1 (.D(mdr_1_q), .LOAD(control_unit_1_mar_load), .CLK(CLK_out), .Q(mar_1_q));
  // Probe on program_counter_1_q
  Program_Counter program_counter_1 (
    .GND(GND), .CLK(CLK_out), .RESET(RESET), .D(multiplexer_1_out), .INC(or_1_out),
    .LOAD(control_unit_1_pc_load), .Q(program_counter_1_q));
  TFSM tfsm_1 (
    .CLK(CLK_out), .RESET(RESET), .T_WE(VCC), .NEEDS2(or_3_out), .T(tfsm_1_t), .FETCH(tfsm_1_fetch),
    .PH2(tfsm_1_ph2));  // open: PH3
  // Probe on mar_1_q
  // Probe on tfsm_1_t
  and and_1 (and_1_out, tfsm_1_ph2, or_3_out);
  Instruction_Memory_ROM instruction_memory_rom_1 (.A(program_counter_1_q), .D(instruction_memory_rom_1_d));
  // Probe on and_1_out
  and and_2 (and_2_out, tfsm_1_fetch, and_4_out);
  // Probe on instruction_memory_rom_1_d
  // Probe on control_unit_1_rsela
  Multiplexer #(.width(8)) multiplexer_2 (
    .in0(memory_ram_1_d_out), .in1(instruction_memory_rom_1_d), .out(multiplexer_2_out), .sel(and_1_out));
  or or_2 (or_2_out, and_1_out, and_2_out);
  // Probe on control_unit_1_rselb
  // Probe on multiplexer_2_out
  Memory_RAM memory_ram_1 (
    .A(mar_1_q), .WE(control_unit_1_mem_we), .CLK(CLK_out), .D_IN(resgister_file_1_bout), .VCC(in_4),
    .D_OUT(memory_ram_1_d_out));
  // Probe on or_2_out
  or or_3 (or_3_out, not_1_out, and_3_out);
  not not_1 (not_1_out, xor_1_out);
  xor xor_1 (xor_1_out, instruction_register_1_ir[4], instruction_register_1_ir[5]);
  and and_3 (and_3_out, instruction_register_1_ir[6], instruction_register_1_ir[7]);
  // Probe on mdr_1_q
  MDR mdr_1 (.D(multiplexer_2_out), .LOAD(or_2_out), .CLK(CLK_out), .Q(mdr_1_q));
  Resgister_File resgister_file_1 (
    .WData(multiplexer_3_out), .CLK(CLK_out), .RESET(RESET), .RSelA(control_unit_1_rsela),
    .ReslB(control_unit_1_rselb), .WSel(control_unit_1_wsel), .WE(control_unit_1_rf_we),
    .AOut(resgister_file_1_aout), .BOut(resgister_file_1_bout));
  Instruction_Register instruction_register_1 (
    .D(instruction_memory_rom_1_d), .LOAD(tfsm_1_fetch), .CLK(CLK_out), .RESET(RESET),
    .IR(instruction_register_1_ir));
  // Probe on resgister_file_1_aout
  // Probe on instruction_register_1_ir
  and and_4 (and_4_out, instruction_register_1_ir[4], instruction_register_1_ir[5], not_2_out, instruction_register_1_ir[7]);
  Multiplexer #(.width(8)) multiplexer_3 (
    .in0(alu_1_y), .in1(mdr_1_q), .out(multiplexer_3_out), .sel(control_unit_1_bsel));
  // Probe on resgister_file_1_bout
  not not_2 (not_2_out, instruction_register_1_ir[6]);
  Multiplexer #(.width(8)) multiplexer_4 (
    .in0(resgister_file_1_bout), .in1(mdr_1_q), .out(multiplexer_4_out), .sel(GND));
  // Probe on multiplexer_4_out
  // Probe on control_unit_1_alu_op
  ALU alu_1 (
    .VCC(VCC), .GND(GND), .A(resgister_file_1_aout), .B(multiplexer_4_out), .OP(control_unit_1_alu_op),
    .Y(alu_1_y), .ZF(alu_1_zf), .NF(alu_1_nf), .CF(alu_1_cf), .OOF(alu_1_oof));
  // Probe on alu_1_y
  Flag_Register flag_register_1 (
    .ZF_IN(alu_1_zf), .NF_IN(alu_1_nf), .CF_IN(alu_1_cf), .OOF_IN(alu_1_oof), .LOAD(control_unit_1_flags_we),
    .CLK(CLK_out), .ZF(flag_register_1_zf));  // open: NF, CF, OOF

  // Notes on the sheet:
  //   VCC: initial=0x1
  //   in_4: initial=0x1
  //   IR_LOAD
  //   needs2
  //   idLDR
endmodule

module ALU (
  input  VCC,
  input  GND,
  input  [7:0] A,
  input  [7:0] B,
  input  [3:0] OP,
  output [7:0] Y,
  output ZF,
  output NF,
  output CF,
  output OOF
);

  wire adder_1_cout, adder_2_cout, adder_3_cout, adder_4_cout, and_2_out, and_3_out, and_4_out, and_5_out,
       not_4_out, not_5_out, not_6_out, not_7_out, not_8_out, not_9_out, or_2_out, or_3_out, or_4_out;
  wire [7:0] adder_1_out, adder_2_out, adder_3_out, adder_4_out, and_1_out, not_1_out, not_2_out, not_3_out,
       or_1_out, xor_1_out;

  assign not_1_out = ~B;  // NOT_Gate not_1, 8 bits wide
  assign not_2_out = ~8'h1;  // NOT_Gate not_2, 8 bits wide
  assign and_1_out = A & B;  // AND_Gate and_1, 8 bits wide
  assign or_1_out = A | B;  // OR_Gate or_1, 8 bits wide
  assign xor_1_out = A ^ B;  // XOR_Gate xor_1, 8 bits wide
  assign not_3_out = ~A;  // NOT_Gate not_3, 8 bits wide
  Adder adder_1 (.a(A), .b(B), .out(adder_1_out), .cin(GND), .cout(adder_1_cout));
  Adder adder_2 (.a(A), .b(not_1_out), .out(adder_2_out), .cin(VCC), .cout(adder_2_cout));
  Adder adder_3 (.a(A), .b(8'h1), .out(adder_3_out), .cin(GND), .cout(adder_3_cout));
  Adder adder_4 (.a(A), .b(not_2_out), .out(adder_4_out), .cin(VCC), .cout(adder_4_cout));
  Multiplexer #(.select(4), .width(8)) multiplexer_1 (
    .in0({8{1'b0}}), .in1(and_1_out), .in2(or_1_out), .in3(xor_1_out), .in4(not_3_out), .in5({A[6:0], A[7]}),
    .in6({A[0], A[7:1]}), .in7({8{1'b0}}), .in8(adder_1_out), .in9(adder_2_out), .in10(adder_3_out),
    .in11(adder_4_out), .in12({8{1'b0}}), .in13({8{1'b0}}), .in14({8{1'b0}}), .in15({8{1'b0}}),
    .out({NF, Y[6:0]}), .sel(OP));
  Multiplexer #(.select(4)) multiplexer_2 (
    .in0(GND), .in1(GND), .in2(GND), .in3(GND), .in4(GND), .in5(A[7]), .in6(A[0]), .in7(GND),
    .in8(adder_1_cout), .in9(adder_2_cout), .in10(adder_3_cout), .in11(adder_4_cout), .in12(GND), .in13(GND),
    .in14(GND), .in15(GND), .out(CF), .sel(OP));
  not not_4 (not_4_out, NF);
  not not_5 (not_5_out, A[7]);
  not not_6 (not_6_out, B[7]);
  not not_7 (not_7_out, NF);
  not not_8 (not_8_out, B[7]);
  not not_9 (not_9_out, A[7]);
  and and_2 (and_2_out, not_4_out, A[7], B[7]);
  and and_3 (and_3_out, NF, not_5_out, not_6_out);
  and and_4 (and_4_out, not_7_out, A[7], not_8_out);
  and and_5 (and_5_out, NF, not_9_out, B[7]);
  or or_2 (or_2_out, and_2_out, and_3_out);
  or or_3 (or_3_out, Y[0], Y[1], Y[2], Y[3], Y[4], Y[5], Y[6], NF);
  or or_4 (or_4_out, and_4_out, and_5_out);
  not not_10 (ZF, or_3_out);
  Multiplexer #(.select(4)) multiplexer_3 (
    .in0(GND), .in1(GND), .in2(GND), .in3(GND), .in4(GND), .in5(GND), .in6(GND), .in7(GND), .in8(or_2_out),
    .in9(or_4_out), .in10(or_2_out), .in11(or_4_out), .in12(GND), .in13(GND), .in14(GND), .in15(GND),
    .out(OOF), .sel(OP));

  assign Y[7] = NF;

  // Notes on the sheet:
  //   VCC: initial=0x1
endmodule

module Resgister_File (
  input  [7:0] WData,
  input  CLK,
  input  RESET,
  input  [1:0] RSelA,
  input  [1:0] ReslB,
  input  [1:0] WSel,
  input  WE,
  output [7:0] AOut,
  output [7:0] BOut
);

  wire AND0_out, AND1_out, AND2_out, AND3_out, decoder_1_out0, decoder_1_out1, decoder_1_out2, decoder_1_out3;
  wire [7:0] R0_q, R1_q, R2_q, R3_q;

  Decoder #(.select(2)) decoder_1 (
    .out0(decoder_1_out0), .out1(decoder_1_out1), .out2(decoder_1_out2), .out3(decoder_1_out3), .sel(WSel));  // open: en
  and AND0 (AND0_out, decoder_1_out0, WE);
  and AND1 (AND1_out, decoder_1_out1, WE);
  and AND2 (AND2_out, decoder_1_out2, WE);
  and AND3 (AND3_out, decoder_1_out3, WE);
  Register R0 (.D(WData), .en(AND0_out), .clk(CLK), .Q(R0_q), .clr(RESET));
  Register R1 (.D(WData), .en(AND1_out), .clk(CLK), .Q(R1_q), .clr(RESET));
  Register R2 (.D(WData), .en(AND2_out), .clk(CLK), .Q(R2_q), .clr(RESET));
  Register R3 (.D(WData), .en(AND3_out), .clk(CLK), .Q(R3_q), .clr(RESET));
  Multiplexer #(.select(2), .width(8)) multiplexer_1 (
    .in0(R0_q), .in1(R1_q), .in2(R2_q), .in3(R3_q), .out(AOut), .sel(RSelA));
  Multiplexer #(.select(2), .width(8)) multiplexer_2 (
    .in0(R0_q), .in1(R1_q), .in2(R2_q), .in3(R3_q), .out(BOut), .sel(ReslB));
endmodule

module Program_Counter (
  input  GND,
  input  CLK,
  input  RESET,
  input  [7:0] D,
  input  INC,
  input  LOAD,
  output [7:0] Q
);

  wire or_1_out;
  wire [7:0] adder_1_out, multiplexer_1_out, multiplexer_2_out;

  Register register_1 (.D(multiplexer_2_out), .en(or_1_out), .clk(CLK), .Q(Q), .clr(RESET));
  or or_1 (or_1_out, LOAD, INC);
  Adder adder_1 (.a(Q), .b(8'h1), .out(adder_1_out), .cin(GND));  // open: cout
  Multiplexer #(.width(8)) multiplexer_1 (.in0(Q), .in1(adder_1_out), .out(multiplexer_1_out), .sel(INC));
  Multiplexer #(.width(8)) multiplexer_2 (.in0(multiplexer_1_out), .in1(D), .out(multiplexer_2_out), .sel(LOAD));
endmodule

module Instruction_Register (
  input  [7:0] D,
  input  LOAD,
  input  CLK,
  input  RESET,
  output [7:0] IR
);

  Register register_1 (.D(D), .en(LOAD), .clk(CLK), .Q(IR), .clr(RESET));
endmodule

module Control_Unit (
  input  [7:0] IR,
  input  ZF,
  input  [1:0] T,
  output [1:0] RSelB,
  output [1:0] RSelA,
  output [3:0] ALU_OP,
  output [1:0] WSel,
  output RF_WE,
  output BSEL,
  output IR_LOAD,
  output PC_INC,
  output PC_LOAD,
  output MAR_LOAD,
  output MDR_LOAD,
  output MEM_WE,
  output FLAGS_WE,
  output NEEDS2
);

  wire and_1_out, and_2_out, and_3_out, and_4_out, and_5_out, and_6_out, and_7_out, and_8_out, and_9_out,
       and_10_out, and_11_out, and_12_out, and_13_out, and_14_out, and_18_out, and_19_out, and_20_out,
       decoder_1_out0, decoder_1_out1, decoder_1_out2, decoder_1_out3, decoder_1_out4, decoder_1_out5,
       decoder_1_out6, decoder_1_out7, decoder_1_out8, decoder_1_out9, decoder_1_out10, decoder_1_out11,
       decoder_1_out12, decoder_1_out13, decoder_1_out14, decoder_1_out15, decoder_2_out0, decoder_2_out1,
       decoder_2_out2, not_1_out, not_2_out, not_4_out, or_1_out, or_2_out, or_4_out, or_5_out;

  not not_1 (not_1_out, T[1]);
  Decoder #(.select(4)) decoder_1 (
    .out0(decoder_1_out0), .out1(decoder_1_out1), .out2(decoder_1_out2), .out3(decoder_1_out3),
    .out4(decoder_1_out4), .out5(decoder_1_out5), .out6(decoder_1_out6), .out7(decoder_1_out7),
    .out8(decoder_1_out8), .out9(decoder_1_out9), .out10(decoder_1_out10), .out11(decoder_1_out11),
    .out12(decoder_1_out12), .out13(decoder_1_out13), .out14(decoder_1_out14), .out15(decoder_1_out15),
    .sel(IR[7:4]));  // open: en
  and and_1 (and_1_out, T[0], not_1_out);
  not not_2 (not_2_out, T[0]);
  and and_2 (and_2_out, not_2_out, T[1]);
  or or_1 (or_1_out, T[0], T[1]);
  or or_2 (or_2_out, decoder_1_out0, decoder_1_out1, decoder_1_out2, decoder_1_out3, decoder_1_out4, decoder_1_out5, decoder_1_out6, decoder_1_out7, decoder_1_out8, decoder_1_out9, decoder_1_out10, decoder_1_out11);
  Decoder #(.select(2)) decoder_2 (
    .out0(decoder_2_out0), .out1(decoder_2_out1), .out2(decoder_2_out2), .sel(IR[3:2]));  // open: out3, en
  and and_3 (and_3_out, decoder_1_out15, decoder_2_out0);
  and and_4 (and_4_out, decoder_1_out15, decoder_2_out1);
  and and_5 (and_5_out, decoder_1_out15, decoder_2_out2);
  not not_3 (IR_LOAD, or_1_out);
  not not_4 (not_4_out, ZF);
  or or_3 (NEEDS2, decoder_1_out12, decoder_1_out15);
  and and_6 (and_6_out, and_4_out, ZF);
  and and_7 (and_7_out, and_5_out, not_4_out);
  and and_8 (and_8_out, or_2_out, and_1_out);
  and and_9 (and_9_out, decoder_1_out12, and_2_out);
  and and_10 (and_10_out, and_1_out, decoder_1_out13);
  or or_4 (or_4_out, and_6_out, and_7_out);
  and and_11 (and_11_out, and_1_out, decoder_1_out13);
  and and_12 (and_12_out, decoder_1_out13, and_2_out);
  and and_13 (and_13_out, decoder_1_out13, and_1_out);
  and and_14 (and_14_out, and_1_out, NEEDS2);
  or or_5 (or_5_out, and_3_out, or_4_out);
  or or_6 (MDR_LOAD, and_13_out, and_14_out);
  or or_7 (RF_WE, and_8_out, and_9_out, and_10_out);
  // AND_Gate and_15 has open pins: in0=or_5_out, in1=and_2_out, in2=decoder_1_out15, out=open
  // OR_Gate or_8 has open pins: in0=IR_LOAD, in1=and_20_out, in2=and_11_out, in3=and_12_out, out=open
  and and_16 (MEM_WE, and_1_out, decoder_1_out14);
  and and_17 (FLAGS_WE, and_1_out, or_2_out);
  or or_9 (BSEL, and_18_out, and_19_out);
  and and_18 (and_18_out, and_1_out, decoder_1_out13);
  and and_19 (and_19_out, decoder_1_out12, and_2_out);
  and and_20 (and_20_out, NEEDS2, and_1_out);
  or or_10 (PC_INC, IR_LOAD, and_20_out);
  and and_21 (MAR_LOAD, and_1_out, decoder_1_out15);
  and and_22 (PC_LOAD, decoder_1_out15, and_2_out);

  assign ALU_OP = IR[7:4];
  assign RSelA = IR[3:2];
  assign RSelB = IR[1:0];
  assign WSel = IR[3:2];

  // Notes on the sheet:
  //   PH2
  //   PH3
  //   EXEC
  //   Jsub
  //   IS_ALU
  //   IS_LDI
  //   IS_LDR
  //   IS_STR
  //   IS_J
  //   sJMP
  //   sJZ
  //   IS_LDR
  //   sJNZ
  //   FETCH
  //   IS_J
  //   JUMP_TAKEN
  //   IMM
endmodule

module Memory_RAM (
  input  [7:0] A,
  input  WE,
  input  CLK,
  input  [7:0] D_IN,
  input  VCC,
  output [7:0] D_OUT
);

  RAM ram_1 (.addr(A), .we(WE), .oe(VCC), .clk(CLK), .din(D_IN), .dout(D_OUT));
endmodule

module Instruction_Memory_ROM (
  input  [7:0] A,
  output [7:0] D
);

  ROM rom_1 (.addr(A), .data(D));

  // Notes on the sheet:
  //   contents of rom_1 (hex, n*v repeats v):
  //   c4 a c2 5 1 11 21 31 41 51 61 81
endmodule

module Flag_Register (
  input  ZF_IN,
  input  NF_IN,
  input  CF_IN,
  input  OOF_IN,
  input  LOAD,
  input  CLK,
  output ZF,
  output NF,
  output CF,
  output OOF
);

  Register #(.width(4)) register_1 (
    .D({ZF_IN, NF_IN, CF_IN, OOF_IN}), .en(LOAD), .clk(CLK), .Q({ZF, NF, CF, OOF}));  // open: clr
endmodule

module MAR (
  input  [7:0] D,
  input  LOAD,
  input  CLK,
  output [7:0] Q
);

  Register register_1 (.D(D), .en(LOAD), .clk(CLK), .Q(Q));  // open: clr
endmodule

module MDR (
  input  [7:0] D,
  input  LOAD,
  input  CLK,
  output [7:0] Q
);

  Register register_1 (.D(D), .en(LOAD), .clk(CLK), .Q(Q));  // open: clr
endmodule

module TFSM (
  input  CLK,
  input  RESET,
  input  T_WE,
  input  NEEDS2,
  output [1:0] T,
  output FETCH,
  output PH2,
  output PH3
);

  wire not_1_out, not_2_out, not_3_out, not_4_out;
  wire [1:0] and_2_out;

  and and_1 (and_2_out[1], NEEDS2, not_1_out, T[0]);
  and and_2 (and_2_out[0], not_1_out, not_2_out);
  Register #(.width(2)) register_1 (.D(and_2_out), .en(T_WE), .clk(CLK), .Q(T), .clr(RESET));
  not not_1 (not_1_out, T[1]);
  not not_2 (not_2_out, T[0]);
  not not_3 (not_3_out, T[0]);
  not not_4 (not_4_out, T[1]);
  and and_3 (FETCH, not_3_out, not_4_out);
  and and_4 (PH2, T[0], not_4_out);
  and and_5 (PH3, T[1], not_3_out);

  // Notes on the sheet:
  //   T_WE: initial=0x1
endmodule
